# Fritzing sketch pcb_001 (saved by Fritzing 0.9.6b)
circuit board: 10cm x 10cm
breadboards: 1

parts:
  J1 = male pin header, 8 pins [form="♂ (male)"]
  U5 = PCF8574 [package="DIP16 [THT]"]
  J4 = double row male pin header, 6 pins [form="♂ (male)"]
  U7 = TLP620-4 [package="DIP (Dual Inline) [THT]"]
  U8 = TLP620-4 [package="DIP (Dual Inline) [THT]"]
  J5 = male pin header, 4 pins [form="♂ (male)"]
  J3 = male pin header, 2 pins [form="♂ (male)"]
  R10 = Resistor [tolerance=±5% resistance=2k power=0.25 package="0603 [SMD]"]
  R11 = Resistor [tolerance=±5% resistance=2k power=0.25 package="0603 [SMD]"]
  R12 = Resistor [tolerance=±5% resistance=2k power=0.25 package="0603 [SMD]"]
  R1 = Resistor [tolerance=±5% resistance=22 power=0.25 package="0603 [SMD]"]
  R2 = Resistor [tolerance=±5% resistance=22 power=0.25 package="0603 [SMD]"]
  R3 = Resistor [tolerance=±5% resistance=22 power=0.25 package="0603 [SMD]"]
  R4 = Resistor [tolerance=±5% resistance=22 power=0.25 package="0603 [SMD]"]
  R5 = Resistor [tolerance=±5% resistance=22 power=0.25 package="0603 [SMD]"]
  R6 = Resistor [tolerance=±5% resistance=22 power=0.25 package="0603 [SMD]"]
  R7 = Resistor [tolerance=±5% resistance=22 power=0.25 package="0603 [SMD]"]
  R8 = Resistor [tolerance=±5% resistance=22 power=0.25 package="0603 [SMD]"]
  R16 = Resistor [tolerance=±5% resistance=2k power=0.25 package="0603 [SMD]"]
  R13 = Resistor [tolerance=±5% resistance=2k power=0.25 package="0603 [SMD]"]
  R14 = Resistor [tolerance=±5% resistance=2k power=0.25 package="0603 [SMD]"]
  R15 = Resistor [tolerance=±5% resistance=2k power=0.25 package="0603 [SMD]"]
  R9 = Resistor [tolerance=±5% resistance=2k power=0.25 package="0603 [SMD]"]

nets:
  N1: J1.pin1, R1.Pin_0, R9.Pin_1
  N2: J1.pin2, R10.Pin_1, R2.Pin_0
  N3: J1.pin3, R11.Pin_1, R3.Pin_0
  N4: J1.pin4, R12.Pin_1, R4.Pin_0
  N5: J1.pin5, R5.Pin_0, R13.Pin_1
  N6: J1.pin6, R6.Pin_0, R14.Pin_1
  N7: J1.pin7, R7.Pin_0, R15.Pin_1
  N8: J1.pin8, R8.Pin_0, R16.Pin_1
  N9: U5.A0, J4.pin6
  N10: U5.A1, J4.pin5
  N11: U5.A2, J4.pin4
  GND: U5.GND, J5.pin4
  N12: U5.SCL, J5.pin3
  N13: U5.SDA, J5.pin2
  N14: U5.VCC, J5.pin1
  N15: J4.pin1, J4.pin2, J4.pin3
  N16: U7.pin1, R1.Pin_1
  N17: U7.pin2, U7.pin4, U7.pin6, U7.pin8, U8.pin2, U8.pin4, U8.pin6, U8.pin8, J3.pin1, J3.pin2, R10.Pin_0, R11.Pin_0, R12.Pin_0, R16.Pin_0, R13.Pin_0, R14.Pin_0, R15.Pin_0, R9.Pin_0
  N18: U7.pin3, R2.Pin_1
  N19: U7.pin5, R3.Pin_1
  N20: U7.pin7, R4.Pin_1
  N21: U8.pin1, R5.Pin_1
  N22: U8.pin3, R6.Pin_1
  N23: U8.pin5, R7.Pin_1
  N24: U8.pin7, R8.Pin_1

custom parts:
  TLP620-4: Quad Photo-transistor optically coupled to two infrared emitting diodes connected in inverse parallel.
